# Fritzing sketch Touch keyboard (saved by Fritzing 0.9.3b)
circuit board: 29.9353cm x 29.9406cm
breadboards: 1

parts:
  Part1 = MPR121 Breakout
  Part2 = MPR121 Breakout

nets:
  GND: Part1.ADDR, Part1.GND, Part2.GND
  N1: Part1.SCL, Part2.SCL
  N2: Part1.SDA, Part2.SDA
  3.3V: Part1.3.3V, Part2.ADDR, Part2.3.3V
