# Fritzing sketch Touch keyboard1 (saved by Fritzing 0.9.3b)
circuit board: 14.7015cm x 7.27801cm
breadboards: 1

parts:
  Part1 = MPR121 Breakout
  J2 = female pin header, 6 pins [form="♀ (female)"]
  J3 = female pin header, 6 pins [form="♀ (female)"]

nets:
  N1: Part1.ADDR, J2.pin5, J3.pin5
  N2: Part1.~IRQ, J2.pin2, J3.pin2
  N3: Part1.SCL, J2.pin3, J3.pin3
  N4: Part1.SDA, J2.pin4, J3.pin4
  N5: Part1.3.3V, J2.pin1, J3.pin1
  N6: Part1.GND, J2.pin6, J3.pin6
